// Digital circuit IPCS.dig as structural Verilog
module IPCS (
  input  [2:0] Schritt,
  input  C,
  input  [15:0] IPin,
  input  [15:0] CSin,
  input  [15:0] DB,
  output [15:0] IPout,
  output [15:0] CSout,
  output [19:0] Adr
);

  wire decoder_1_out_0, decoder_1_out_4, decoder_1_out_5, decoder_1_out_6, or_1_out, or_2_out, or_3_out;
  wire [15:0] driver_1_out, driver_2_out;
  wire [19:0] offsetadd_1_seg_plus_off;

  assign driver_1_out = decoder_1_out_0 ? IPin : 16'bz;  // Driver driver_1
  assign driver_2_out = decoder_1_out_0 ? CSin : 16'bz;  // Driver driver_2
  assign driver_1_out = decoder_1_out_4 ? DB : 16'bz;  // Driver driver_3
  assign driver_2_out = decoder_1_out_5 ? DB : 16'bz;  // Driver driver_4
  Decoder #(.Selector_Bits(3)) decoder_1 (
    .sel(Schritt), .out_0(decoder_1_out_0), .out_4(decoder_1_out_4), .out_5(decoder_1_out_5),
    .out_6(decoder_1_out_6));  // open: out_1, out_2, out_3, out_7
  or or_1 (or_1_out, decoder_1_out_5, decoder_1_out_6);
  or or_2 (or_2_out, decoder_1_out_0, decoder_1_out_4);
  or or_3 (or_3_out, decoder_1_out_0, decoder_1_out_5);
  Register #(.Bits(16)) register_1 (.D(driver_1_out), .C(C), .en(or_2_out), .Q(IPout));
  Register #(.Bits(16)) register_2 (.D(driver_2_out), .C(C), .en(or_3_out), .Q(CSout));
  Offsetadd offsetadd_1 (.Pointer(IPout), .Segment(CSout), .Seg_plus_Off(offsetadd_1_seg_plus_off));
  assign Adr = or_1_out ? offsetadd_1_seg_plus_off : 20'bz;  // Driver driver_5

  // Notes on the sheet:
  //   Schritt: Aktueller Schritt in der Simulation
  //   Adr: Fortsetzadresse (Adresse, an der die ISR steht)
  //   IPin: default 45054
  //   CSin: default 4660
  //   Hold Adr on High-Z 
  //   until step 5
endmodule
