// Digital circuit Main_Interruptverarbeitung_8086.dig as structural Verilog
module Main_Interruptverarbeitung_8086 (
  input  [15:0] IP,
  input  [15:0] CS,
  input  [15:0] SS,
  input  [15:0] SP,
  input  Clock,
  output [15:0] IP_2,
  output [15:0] CS_2,
  output [15:0] out_5,
  output [15:0] out_6,
  output [15:0] out_7,
  output [15:0] out_8,
  output [15:0] out_9,
  output [15:0] out_10,
  output [15:0] out_11,
  output [19:0] out_12,
  output [19:0] out_13,
  output [19:0] out_14,
  output [19:0] Stack_Adresse,
  output [19:0] Adresse_der_ISR
);

  wire _0, _1, _2, _3, _4, _5, _6, _7, EN, INT0_p1, INT1_p1, INT2_p1, INT3_p1, INT4_p1, INT5_p1, INT6_p1,
       INT7_p1, interruptcontroller_1_intr, Louder, Next, Prev, prozessor_1_inta, prozessor_1_rd,
       prozessor_1_wr, Quiet, S0, S1, S2, S3, S4, S5, S6, S7;
  wire [3:0] Schritt;
  wire [7:0] RAM_d;
  wire [15:0] DB;
  wire [19:0] AB, barrelshifter_1_out, ram_control_1_a;

  LED led_1 (.in(S0));
  LED led_2 (.in(S1));
  LED led_3 (.in(S2));
  LED led_4 (.in(S3));
  LED led_5 (.in(S4));
  LED led_6 (.in(S5));
  LED led_7 (.in(S6));
  BarrelShifter #(.Bits(20)) barrelshifter_1 (.in({4'b0000, SS}), .shift(5'b00100), .out(barrelshifter_1_out));
  Add #(.Bits(20)) add_1 (.a({4'b0000, SP}), .b(barrelshifter_1_out), .c_i(1'b0), .s(Stack_Adresse));  // open: c_o
  LED led_8 (.in(S0));
  LED led_9 (.in(S1));
  LED led_10 (.in(S2));
  LED led_11 (.in(S3));
  LED led_12 (.in(S4));
  LED led_13 (.in(S5));
  LED led_14 (.in(S6));
  // ButtonLED INT0: pin names not known; wires that end beside it: INT0_p1, _0
  // ButtonLED INT1: pin names not known; wires that end beside it: INT1_p1, _1
  // ButtonLED INT2: pin names not known; wires that end beside it: INT2_p1, _2
  // ButtonLED INT3: pin names not known; wires that end beside it: INT3_p1, _3
  // ButtonLED INT4: pin names not known; wires that end beside it: INT4_p1, _4
  // ButtonLED INT5: pin names not known; wires that end beside it: INT5_p1, _5
  // ButtonLED INT6: pin names not known; wires that end beside it: INT6_p1, _6
  // ButtonLED INT7: pin names not known; wires that end beside it: INT7_p1, _7
  // ButtonLED DOWN: pin names not known; wires that end beside it: Next, EN
  LED INTR (.in(interruptcontroller_1_intr));
  Interruptcontroller interruptcontroller_1 (
    .INTA(prozessor_1_inta), .INT_0(INT0_p1), .INT_1(INT1_p1), .INT_2(INT2_p1), .INT_3(INT3_p1),
    .INT_4(INT4_p1), .INT_5(INT5_p1), .INT_6(INT6_p1), .INT_7(INT7_p1), .INTR(interruptcontroller_1_intr),
    .DB(DB), ._0(_0), ._1(_1), ._2(_2), ._3(_3), ._4(_4), ._5(_5), ._6(_6), ._7(_7), .EN(EN));
  Prozessor prozessor_1 (
    .C(Clock), .IP_In(IP), .CS_In(CS), .SAdr_In(Stack_Adresse), .DB(DB), .Next(Next), .Prev(Prev),
    .INTR(interruptcontroller_1_intr), .AB(AB), .WR(prozessor_1_wr), .RD(prozessor_1_rd), .IP_out(IP_2),
    .CS_Out(CS_2), .Adr_ISR(Adresse_der_ISR), .Schritt(Schritt), .INTA(prozessor_1_inta));  // open: SAdr_Out
  // ButtonLED UP: pin names not known; wires that end beside it: Prev, EN
  LED INTA (.in(prozessor_1_inta));
  Button LEFT (.out(Quiet));
  Button RIGHT (.out(Louder));
  LED Schreiben (.in(prozessor_1_wr));
  LED Lesen (.in(prozessor_1_rd));
  // Misc misc_1: pin names not known; wires that end beside it: out_11, DB, out_5, AB, out_6, Next, out_7, Prev, out_8, Schritt, out_9, Clock, out_10, Quiet, S7, Louder, S6, EN, S5, S4, S3, S2, S1, S0, out_12, out_13, out_14
  RAM_Control ram_control_1 (
    .C(Clock), .AB(AB), .WR(prozessor_1_wr), .RD(prozessor_1_rd), .DB(DB), .D(RAM_d), .A(ram_control_1_a));
  RAMSinglePort #(.AddrBits(20), .Bits(8)) RAM (
    .A(ram_control_1_a), .str(prozessor_1_wr), .C(Clock), .ld(prozessor_1_rd), .D(RAM_d));

  // Other names for the same wires on the sheet: A6[19:0] = out_12; A8[19:0] = out_13; A10[19:0] = out_14;
  //   Adr[19:0] = Adresse_der_ISR; C = Clock; CSi[15:0] = CS; CSo[15:0] = CS_2; D2[15:0] = out_11; D4[15:0] = out_5;
  //   D6[15:0] = out_6; D8[15:0] = out_7; D10[15:0] = out_8; D22[15:0] = out_9; D24[15:0] = out_10; IPi[15:0] = IP;
  //   IPo[15:0] = IP_2

  // Notes on the sheet:
  //   IP: Initialisierter Wert von IP: Instruction Pointer (16-Bit-Befehlszeiger)
  //   ACHTUNG! Der Wert hier dient nur der Initialisierung.
  //   Er wird während der Simulation nicht automatisch geändert.
  //   Für den in der Simulation aktuellen Wert von IP, bitte 'IP' in Aktulle Registerinhalte überprüfen., default 45054
  //   CS: Initialisierter Wert von CS: Code-Segment (16-Bit-Befehlszeiger)
  //   ACHTUNG! Der Wert hier dient nur der Initialisierung.
  //   Er wird während der Simulation nicht automatisch geändert.
  //   Für den in der Simulation aktuellen Wert von CS, bitte 'CS' in Aktulle Registerinhalte überprüfen.
  //   Aus Wikipedia:
  //   Das Codesegment ist der Teil eines Anwendungsprogramms, in dem die expliziten Maschinen-Codes (Opcodes) stehen, die an den Prozessor geleitet und dann ausgeführt werden. Ein Codesegment enthält also Anweisungen (Befehle) für den Rechner, die dieser ausführen soll.
  //   Das Codesegment wird vom Compiler aus dem Quellcode der Anwendung übersetzt. Aus dem Codesegment kann man mit Hilfe eines Disassemblers wieder Quellcode (Assembler-Code) zurückgewinnen. Der Begriff „Codesegment“ bezeichnet sowohl den Anweisungsbereich in der Programmdatei, als auch den Bereich des Arbeitsspeichers mit dem zur Ausführung geladenen Programm.
  //   Nach dem Laden des Programms durch das Betriebssystem arbeitet der Prozessor die Befehle im Codesegment Schritt für Schritt ab, bis in der Anwendung eine Abbruchbedingung eintritt, die die Beendigung der Anwendung einleitet., default 4660
  //   IP_2: Aktueller Wert von IP: Instruction Pointer (16-Bit-Befehlszeiger)
  //   IP zeigt auf die Adresse, die die nächste Anweisung für den 
  //   Prozessor enthält. Nach einem Interrupt
  //   CS_2: Aktueller Wert von CS: Code-Segment (16-Bit-Befehlszeiger)
  //   Aus Wikipedia:
  //   Das Codesegment ist der Teil eines Anwendungsprogramms, in dem die expliziten Maschinen-Codes (Opcodes) stehen, die an den Prozessor geleitet und dann ausgeführt werden. Ein Codesegment enthält also Anweisungen (Befehle) für den Rechner, die dieser ausführen soll.
  //   Das Codesegment wird vom Compiler aus dem Quellcode der Anwendung übersetzt. Aus dem Codesegment kann man mit Hilfe eines Disassemblers wieder Quellcode (Assembler-Code) zurückgewinnen. Der Begriff „Codesegment“ bezeichnet sowohl den Anweisungsbereich in der Programmdatei, als auch den Bereich des Arbeitsspeichers mit dem zur Ausführung geladenen Programm.
  //   Nach dem Laden des Programms durch das Betriebssystem arbeitet der Prozessor die Befehle im Codesegment Schritt für Schritt ab, bis in der Anwendung eine Abbruchbedingung eintritt, die die Beendigung der Anwendung einleitet.
  //   out_5: Datenbus mit 4 Clock-Ticks Verzögerung
  //   out_6: Datenbus mit 6 Clock-Ticks Verzögerung
  //   out_7: Datenbus mit 8 Clock-Ticks Verzögerung
  //   out_8: Datenbus mit 8 Clock-Ticks Verzögerung
  //   out_9: Datenbus vom Interruptcontroller zum Prozessor
  //   mit 2 Clock-Ticks Verzögerung
  //   out_10: Datenbus mit 8 Clock-Ticks Verzögerung
  //   out_11: Datenbus mit 2 Clock-Ticks Verzögerung
  //   out_12: Adressbus mit 2 Clock-Ticks Verzögerung
  //   out_13: Adressbus mit 2 Clock-Ticks Verzögerung
  //   out_14: Adressbus mit 2 Clock-Ticks Verzögerung
  //   SS: Das Stack-Segment-Register (SS) wird benutzt, um das RAM-Segment zu speichern, 
  //   das den Call-Stack the aktuell ausgeführten Programms enthält.
  //   SP: Der Stack-Pointer is das Haupt-Stack-Register des 8086., default 36
  //   Stack_Adresse: Die Stack-Adresse entsteht durch Schieben des Stack-Segments (SS) um eine Stelle nach links (=Multiplikation mit 10hex) und anschließendes Addieren des Stack-Pointers (SP).
  //   Wenn beispielsweise das Stack-Segment (SS) die Adresse 1234hex und der Stack-Pointer die Adresse 5678hex enthält, dann ist die Stack-Adresse: 
  //   1234hex × 10hex + 5678hex = 
  //   12340hex + 5678hex = 
  //   179B8hex
  //   Adresse_der_ISR: Dies ist die Adresse der Interrupt-Service-Routine (ISR), 
  //   an die der 8086 nach einem Interrupt springt.
  //   Clock: Hz: 400
  //   -
  //   Zuerst Interrupt auswählen!
  //   Schritt 1: Register IP auf den Stack legen (PUSH IP)
  //   Schritt 2: Register CS auf den Stack legen (PUSH CS)
  //   Schritt 3: Aufnahme der Interruptnummer
  //   Schritt 4: Aufnahme von IP aus der Vektortabelle
  //   Schritt 5: Aufnahme von CS aus der Vektortabelle
  //   Nach Schritt 5 kennt der 8086 die Adresse der 
  //   Interrupt-Service-Routine (ISR), an der er fortfahren wird:
  //   Schritt 6: Interrupt-Service-Routine (ISR) wird ausgeführt
  //   Initialisierung der Registerinhalte
  //   Aktuelle Registerinhalte
  //   Hier Interrupt 
  //   auswählen:
  //   Einzelschrittmodus
  //   Pfeil-runter-Taste: Schritt vorwärts
  //   Pfeil-hoch-Taste: Schritt zurück
  //   Simulation der Interruptverarbeitung des Intel 8086 Prozessors
  //   Ton
  //   Lautstärke der Simulation eingestellen.
  //   Pfeil-links-Taste auf der Tastatur: leiser
  //   Pfeil-rechts-Taste auf der Tastatur: lauter
  //   Adressbus (20 Bit)
  //   Datenbus (16 Bit)
  //   Während der Simulation kann der RAM durch Klick 
  //   auf den Baustein ausgelesen und beschrieben werden.
  //   Das "Play-Symbols" oben (oder die Leertaste) starten die Simulation.
  //   Der 8086 spielt beispielhaft Billie Jean von Michael Jackson,
  //   um einen normalen Programmablauf zu simulieren.
  //   Unterbricht man ihn mit einem Interrupt, hört er auf Billie Jean zu spielen.
  //   Dann kann man die Interruptverarbeitung in Schritten simulieren.
  //   Random Access Memory (RAM)
  //   Audio & Optik
endmodule
