// Digital circuit Misc.dig as structural Verilog
// Dieses Bauteil dient nur der Optik. Es sorgt dafür, dass die LED am korrekten Schritt an ist und dafür, dass sich Daten auf Datenbus und Adressbus "langsam und in die richtige Richtung" fortbewegen.
module Misc (
  input  [15:0] DB,
  input  [19:0] AB,
  input  Next,
  input  Prev,
  input  [2:0] Schritt,
  input  _400Hz,
  input  Quiet,
  input  Louder,
  input  EN,
  output [15:0] D25,
  output [15:0] D27,
  output [15:0] D29,
  output [15:0] D31,
  output [15:0] D33,
  output [15:0] D45,
  output [15:0] D47,
  output S15,
  output S14,
  output S13,
  output S12,
  output S11,
  output S10,
  output S9,
  output S8,
  output [19:0] A11,
  output [19:0] A13,
  output [19:0] A15
);

  wire _0_78125Hz, _1_5625Hz, _3_125Hz, _6_25Hz, _12_5Hz, _25Hz, _50Hz, _100Hz, _200Hz, and_1_out, and_2_out,
       Clk_ISR, D0, decoder_2_out_1, decoder_2_out_2, decoder_2_out_3, decoder_2_out_4, decoder_2_out_5,
       decoder_2_out_6, decoder_2_out_7, decoder_3_out_1, decoder_3_out_2, decoder_3_out_3, decoder_3_out_4,
       decoder_3_out_5, decoder_3_out_6, decoder_3_out_7, decoder_4_out_0, decoder_4_out_1, decoder_4_out_2,
       decoder_4_out_3, decoder_4_out_4, decoder_4_out_5, decoder_4_out_6, decoder_4_out_7, not_1_out,
       Only_allow_Louder_when_Volume_lt_0x70_lt, Only_allow_Quieter_when_Volume_gt_0_gt, or_1_out, or_2_out,
       or_3_out, or_4_out, or_5_out, or_6_out, rs_ff_as_1_q;
  wire [2:0] _1Hz_Clk_counter_out, Clock_Counter_out, Save_InterruptNr_on_Step_3__no_change_in_Step_3_q,
       step_counter_1_step;
  wire [6:0] Standard_Volume_is_middle_0x36_s;

  or or_1 (or_1_out, S9, S10);
  or or_2 (or_2_out, S12, S13);
  or or_3 (or_3_out, Next, Prev);
  or or_4 (or_4_out, or_1_out, or_2_out);
  Decoder #(.Selector_Bits(3)) decoder_1 (
    .sel(Schritt), .out_0(S8), .out_1(S9), .out_2(S10), .out_3(S11), .out_4(S12), .out_5(S13), .out_6(S14),
    .out_7(S15));
  RS_FF_AS rs_ff_as_1 (.S(or_3_out), .R(D0), .Q(rs_ff_as_1_q));  // open: nQ
  CounterPreset #(.Bits(3)) _1Hz_Clk_counter (
    .en(or_4_out), .C(_0_78125Hz), .dir(or_2_out), .in(3'b000), .ld(1'b0), .clr(rs_ff_as_1_q),
    .out(_1Hz_Clk_counter_out));  // open: ovf
  assign A13 = or_5_out ? AB : 20'bz;  // Driver driver_1
  assign A15 = or_5_out ? AB : 20'bz;  // Driver driver_2
  Counter #(.Bits(3)) Clock_Counter (.en(S11), .C(_0_78125Hz), .clr(~S11), .out(Clock_Counter_out));  // open: ovf
  assign D25 = or_6_out ? DB : 16'bz;  // Driver driver_3
  assign A11 = or_5_out ? AB : 20'bz;  // Driver driver_4
  assign D27 = or_6_out ? DB : 16'bz;  // Driver driver_5
  assign D29 = or_6_out ? DB : 16'bz;  // Driver driver_6
  assign D25 = or_5_out ? DB : 16'bz;  // Driver driver_7
  assign D27 = or_5_out ? DB : 16'bz;  // Driver driver_8
  assign A15 = decoder_3_out_5 ? AB : 20'bz;  // Driver driver_9
  assign D45 = or_6_out ? DB : 16'bz;  // Driver driver_10
  assign D47 = or_6_out ? DB : 16'bz;  // Driver driver_11
  assign D29 = or_5_out ? DB : 16'bz;  // Driver driver_12
  assign D31 = or_5_out ? DB : 16'bz;  // Driver driver_13
  assign D33 = decoder_3_out_5 ? DB : 16'bz;  // Driver driver_14
  assign D31 = decoder_3_out_4 ? DB : 16'bz;  // Driver driver_15
  or or_5 (or_5_out, decoder_3_out_6, decoder_3_out_7);
  assign D33 = or_5_out ? DB : 16'bz;  // Driver driver_16
  or or_6 (or_6_out, decoder_2_out_6, decoder_2_out_7);
  assign D25 = decoder_2_out_5 ? DB : 16'bz;  // Driver driver_17
  assign A13 = decoder_3_out_4 ? AB : 20'bz;  // Driver driver_18
  Decoder #(.Selector_Bits(3)) decoder_2 (
    .sel(Clock_Counter_out), .out_1(decoder_2_out_1), .out_2(decoder_2_out_2), .out_3(decoder_2_out_3),
    .out_4(decoder_2_out_4), .out_5(decoder_2_out_5), .out_6(decoder_2_out_6), .out_7(decoder_2_out_7));  // open: out_0
  assign D29 = decoder_2_out_3 ? DB : 16'bz;  // Driver driver_19
  assign D27 = decoder_2_out_4 ? DB : 16'bz;  // Driver driver_20
  assign D27 = decoder_2_out_5 ? DB : 16'bz;  // Driver driver_21
  Decoder #(.Selector_Bits(3)) decoder_3 (
    .sel(_1Hz_Clk_counter_out), .out_0(D0), .out_1(decoder_3_out_1), .out_2(decoder_3_out_2),
    .out_3(decoder_3_out_3), .out_4(decoder_3_out_4), .out_5(decoder_3_out_5), .out_6(decoder_3_out_6),
    .out_7(decoder_3_out_7));
  assign D25 = decoder_3_out_1 ? DB : 16'bz;  // Driver driver_22
  assign D27 = decoder_3_out_2 ? DB : 16'bz;  // Driver driver_23
  assign D29 = decoder_3_out_3 ? DB : 16'bz;  // Driver driver_24
  assign A11 = decoder_3_out_3 ? AB : 20'bz;  // Driver driver_25
  assign D45 = decoder_2_out_1 ? DB : 16'bz;  // Driver driver_26
  assign D47 = decoder_2_out_2 ? DB : 16'bz;  // Driver driver_27
  assign D47 = decoder_2_out_3 ? DB : 16'bz;  // Driver driver_28
  assign D29 = decoder_2_out_4 ? DB : 16'bz;  // Driver driver_29
  assign D29 = decoder_2_out_5 ? DB : 16'bz;  // Driver driver_30
  assign D45 = decoder_2_out_2 ? DB : 16'bz;  // Driver driver_31
  assign D47 = decoder_2_out_4 ? DB : 16'bz;  // Driver driver_32
  assign D45 = decoder_2_out_3 ? DB : 16'bz;  // Driver driver_33
  assign D45 = decoder_2_out_4 ? DB : 16'bz;  // Driver driver_34
  assign D47 = decoder_2_out_5 ? DB : 16'bz;  // Driver driver_35
  assign D45 = decoder_2_out_5 ? DB : 16'bz;  // Driver driver_36
  and and_1 (and_1_out, Only_allow_Louder_when_Volume_lt_0x70_lt, Louder);
  and and_2 (and_2_out, Quiet, Only_allow_Quieter_when_Volume_gt_0_gt);
  Counter #(.Bits(9)) Clock_Counter_2 (
    .en(1'b1), .C(_400Hz), .clr(1'b0),
    .out({_0_78125Hz, _1_5625Hz, _3_125Hz, _6_25Hz, _12_5Hz, _25Hz, _50Hz, _100Hz, _200Hz}));  // open: ovf
  Step_counter step_counter_1 (.Next(and_1_out), .Prev(and_2_out), .en(1'b1), .Step(step_counter_1_step));
  D_FF #(.Bits(3)) Save_InterruptNr_on_Step_3__no_change_in_Step_3 (
    .D(DB[2:0]), .C(S11), .Q(Save_InterruptNr_on_Step_3__no_change_in_Step_3_q));  // open: nQ
  assign Clk_ISR = decoder_4_out_4 ? _12_5Hz : 1'bz;  // Driver driver_37
  assign Clk_ISR = decoder_4_out_5 ? _50Hz : 1'bz;  // Driver driver_38
  Add #(.Bits(7)) Standard_Volume_is_middle_0x36 (
    .a({step_counter_1_step, 4'b0000}), .b(7'b0110000), .c_i(1'b0), .s(Standard_Volume_is_middle_0x36_s));  // open: c_o
  assign Clk_ISR = decoder_4_out_6 ? _100Hz : 1'bz;  // Driver driver_39
  Comparator #(.Bits(7)) Only_allow_Louder_when_Volume_lt_0x70 (
    .a(Standard_Volume_is_middle_0x36_s), .b(7'b1110000), .lt(Only_allow_Louder_when_Volume_lt_0x70_lt));  // open: gt, eq
  Comparator #(.Bits(7)) Only_allow_Quieter_when_Volume_gt_0 (
    .a(Standard_Volume_is_middle_0x36_s), .b({7{1'b0}}), .gt(Only_allow_Quieter_when_Volume_gt_0_gt));  // open: eq, lt
  assign Clk_ISR = decoder_4_out_7 ? _200Hz : 1'bz;  // Driver driver_40
  Decoder #(.Selector_Bits(3)) decoder_4 (
    .sel(Save_InterruptNr_on_Step_3__no_change_in_Step_3_q), .out_0(decoder_4_out_0),
    .out_1(decoder_4_out_1), .out_2(decoder_4_out_2), .out_3(decoder_4_out_3), .out_4(decoder_4_out_4),
    .out_5(decoder_4_out_5), .out_6(decoder_4_out_6), .out_7(decoder_4_out_7));
  assign Clk_ISR = decoder_4_out_0 ? _1_5625Hz : 1'bz;  // Driver driver_41
  not not_1 (not_1_out, EN);
  assign Clk_ISR = decoder_4_out_1 ? _3_125Hz : 1'bz;  // Driver driver_42
  BillieJean billiejean_1 (.C(_400Hz), .en(not_1_out), .Vol(Standard_Volume_is_middle_0x36_s));
  ISR isr_1 (.en(S14), .C(Clk_ISR), .Vol(Standard_Volume_is_middle_0x36_s));
  assign Clk_ISR = decoder_4_out_2 ? _3_125Hz : 1'bz;  // Driver driver_43
  assign Clk_ISR = decoder_4_out_3 ? _6_25Hz : 1'bz;  // Driver driver_44

  // Other names for the same wires on the sheet: A6[19:0] = A11; A8[19:0] = A13; A10[19:0] = A15; D2[15:0] = D25;
  //   D4[15:0] = D27; D6[15:0] = D29; D8[15:0] = D31; D10[15:0] = D33; D22[15:0] = D45; D24[15:0] = D47; S0 = S8;
  //   S1 = S9; S2 = S10; S3 = S11; S4 = S12; S5 = S13; S6 = S14; S7 = S15

  // Notes on the sheet:
  //   _400Hz: Hz: 400
  //   Step 1&2: PUSH IP & CS
  //   Step 4&5: Aufnahme von IP & CS aus der Vektortabelle
  //   Step 3: Output INTR Number to Data Bus
  //   Clock Divider
endmodule
