// Digital circuit Prozessor.dig as structural Verilog
// Dieses Bauteil ist eine Nachbildung der
// Interruptverarbeitungsfunktionen eines Intel 8086 Prozessors.
module Prozessor (
  input  C,
  input  [15:0] IPi,
  input  [15:0] CSi,
  input  [19:0] SAdr,
  input  [15:0] DB,
  input  Next,
  input  Prev,
  input  INTR,
  output [19:0] AB,
  output WR,
  output RD,
  output [15:0] IPo,
  output [15:0] CSo,
  output [19:0] Adr,
  output [2:0] Schritt,
  output INTA
);

  wire _0, _3, decoder_1_out_1, decoder_1_out_2, decoder_1_out_4, decoder_1_out_5, decoder_1_out_7,
       Save_INTR_q;
  wire [19:0] add_1_s, driverinvsel_1_out, Hold_AB_to_prevent_oscillation_q, Save_InterruptNr_x4_on_Step_3_q,
       sub_1_s;
  wire [31:0] InterruptNr_x4_mul;

  RS_FF_AS Save_INTR (.S(INTR), .R(1'b0), .Q(Save_INTR_q));  // open: nQ
  Step_counter step_counter_1 (.Next(Next), .Prev(Prev), .en(Save_INTR_q), .Step(Schritt));
  Mul #(.Bits(16)) InterruptNr_x4 (.a(DB), .b(16'h4), .mul(InterruptNr_x4_mul));
  IPCS ipcs_1 (.Schritt(Schritt), .C(C), .IPin(IPi), .CSin(CSi), .DB(DB), .IPout(IPo), .CSout(CSo), .Adr(Adr));
  Register #(.Bits(20)) Save_InterruptNr_x4_on_Step_3 (
    .D(InterruptNr_x4_mul[19:0]), .C(C), .en(_3), .Q(Save_InterruptNr_x4_on_Step_3_q));
  Stop stop_1 (.stop(decoder_1_out_7));
  assign DB = decoder_1_out_2 ? CSo : 16'bz;  // Driver driver_1
  Decoder #(.Selector_Bits(3)) decoder_1 (
    .sel(Schritt), .out_0(_0), .out_1(decoder_1_out_1), .out_2(decoder_1_out_2), .out_3(_3),
    .out_4(decoder_1_out_4), .out_5(decoder_1_out_5), .out_7(decoder_1_out_7));  // open: out_6
  assign driverinvsel_1_out = ~decoder_1_out_2 ? SAdr : 20'bz;  // DriverInvSel driverinvsel_1
  assign DB = decoder_1_out_1 ? IPo : 16'bz;  // Driver driver_2
  Add #(.Bits(20)) add_1 (.a(Save_InterruptNr_x4_on_Step_3_q), .b(20'h2), .c_i(1'b0), .s(add_1_s));  // open: c_o
  D_FF #(.Bits(20)) Hold_AB_to_prevent_oscillation (
    .D(AB), .C(decoder_1_out_2), .Q(Hold_AB_to_prevent_oscillation_q));  // open: nQ
  assign AB = decoder_1_out_4 ? Save_InterruptNr_x4_on_Step_3_q : 20'bz;  // Driver driver_3
  assign driverinvsel_1_out = decoder_1_out_2 ? Hold_AB_to_prevent_oscillation_q : 20'bz;  // Driver driver_4
  assign AB = decoder_1_out_5 ? add_1_s : 20'bz;  // Driver driver_5
  Sub #(.Bits(20)) sub_1 (.a(driverinvsel_1_out), .b(20'h2), .c_i(1'b0), .s(sub_1_s));  // open: c_o
  assign AB = WR ? sub_1_s : 20'bz;  // Driver driver_6
  or or_1 (WR, decoder_1_out_1, decoder_1_out_2);
  or or_2 (RD, decoder_1_out_4, decoder_1_out_5);
  not not_1 (INTA, _3);

  // Other names for the same wires on the sheet: S1_OR_S2 = WR

  // Notes on the sheet:
  //   C: Hz: 400
  //   IPi: default 4660
  //   CSi: default 45054
  //   SAdr: Stack-Adresse, berechnet aus SS und SP, default 36
  //   AB: Adressbus
  //   DB: Datenbus
  //   Adr: Fortsetzadresse (Adresse, an der die ISR steht)
  //   Schritt: Aktueller Schritt in der Simulation
  //   Next: Go to next step
  //   Prev: Go to previous step
  //   INTR: Anschluss 18
  //   Dieser Interrupt-Anschluss wird nach dem Abschluss eines jeden Befehls abgetastet, um zu
  //   ermitteln, ob eine Interrupt-Anforderung durch einen Hardware-Baustein vorliegt. Die Abtastung kann durch ein gelöschtes Interrupt Flag verhindert (maskiert) werd
  //   Step 2: DB = CS
  //   en is set to 3 to only output on Step 3
  //   later steps will use DB for RAM & IPCS
  //   and we don't want to interfere with that
  //   Step 1: DB = IP
  //   Step 4: AB = InterruptNr x4
  //   Step 5: AB = InterruptNr x4 + 2
endmodule
