// Digital circuit Step_counter.dig as structural Verilog
module Step_counter (
  input  Next,
  input  Prev,
  input  en,
  output [2:0] Step
);

  wire or_1_out;

  or or_1 (or_1_out, Next, Prev);
  CounterPreset #(.maxValue(7), .Bits(3)) Step_counter (
    .en(en), .C(or_1_out), .dir(Prev), .in(3'b000), .ld(1'b0), .clr(1'b0), .out(Step));  // open: ovf

  // Notes on the sheet:
  //   Next: Go to next step
  //   Prev: Go to previous step
  //   en: Step counter enable, default 1
endmodule
